# Fritzing sketch Setup V2 (saved by Fritzing 0.9.4)
breadboards: 1

parts:
  Bauteil2 = Arduino Nano (Rev3.0)
  9G_Servo = Basic Servo
  Bauteil3 = Adafruit MAX4466 Electret Microphone Amplifier [part_number="Adafruit #1063"]
  Bauteil4 = Adafruit MAX4466 Electret Microphone Amplifier [part_number="Adafruit #1063"]
  Bauteil5 = Adafruit MAX4466 Electret Microphone Amplifier [part_number="Adafruit #1063"]
  Bauteil6 = Adafruit MAX4466 Electret Microphone Amplifier [part_number="Adafruit #1063"]
  Bauteil7 = Adafruit MAX4466 Electret Microphone Amplifier [part_number="Adafruit #1063"]
  Bauteil8 = Arduino Nano (Rev3.0)
  1000uF = Capacitor Polarized [package=cpol-radial-1000uf-25v]
  C1 = Electrolytic Capacitor [capacitance=0.47mF voltage=50V package="0405 [SMD, electrolytic]"]
  C2 = Electrolytic Capacitor [capacitance=0.47mF voltage=50V package="0405 [SMD, electrolytic]"]
  R1 = Resistor [tolerance=±5% resistance=68 package=THT]
  R2 = Resistor [tolerance=±5% resistance=68 package=THT]
  C3 = Electrolytic Capacitor [capacitance=0.47mF voltage=50V package="0405 [SMD, electrolytic]"]
  C4 = Electrolytic Capacitor [capacitance=0.47mF voltage=50V package="0405 [SMD, electrolytic]"]
  C5 = Electrolytic Capacitor [capacitance=0.47mF voltage=50V package="0405 [SMD, electrolytic]"]
  R3 = Resistor [tolerance=±5% resistance=68 package=THT]
  R4 = Resistor [tolerance=±5% resistance=68 package=THT]
  R5 = Resistor [tolerance=±5% resistance=68 package=THT]

nets:
  N1: Bauteil2.D1/TX, Bauteil8.D1/TX
  N2: Bauteil2.D0/RX, Bauteil8.D0/RX
  N3: Bauteil2.RESET, Bauteil8.RESET
  GND: Bauteil2.GND, 9G_Servo.gnd, Bauteil3.GND, Bauteil4.GND, Bauteil5.GND, Bauteil6.GND, Bauteil7.GND, Bauteil8.GND, 1000uF.-, C1.-, C2.-, C3.-, C4.-, C5.-
  N4: Bauteil2.D2, Bauteil8.D2
  N5: Bauteil2.D3, Bauteil8.D3
  N6: Bauteil2.D4, Bauteil8.D4
  N7: Bauteil2.D5, 9G_Servo.pulse, Bauteil8.D5
  N8: Bauteil2.D6, Bauteil8.D6
  N9: Bauteil2.D7, Bauteil8.D7
  N10: Bauteil2.D8, Bauteil8.D8
  N11: Bauteil2.D9, Bauteil8.D9
  N12: Bauteil2.D10, Bauteil8.D10
  N13: Bauteil2.D11/MOSI, Bauteil8.D11/MOSI
  N14: Bauteil2.D12/MISO, Bauteil8.D12/MISO
  VIN: Bauteil2.VIN, Bauteil8.VIN
  VCC: Bauteil2.5V, 9G_Servo.vcc, Bauteil3.VCC, Bauteil4.VCC, Bauteil5.VCC, Bauteil6.VCC, Bauteil7.VCC, Bauteil8.5V, 1000uF.+
  N15: Bauteil2.A7, Bauteil8.A7
  N16: Bauteil2.A6, Bauteil8.A6, C5.+, R3.Pin_1
  N17: Bauteil2.A5, Bauteil8.A5
  N18: Bauteil2.A4, Bauteil8.A4
  N19: Bauteil2.A3, Bauteil8.A3, C4.+, R4.Pin_1
  N20: Bauteil2.A2, Bauteil8.A2, R2.Pin_0, C3.+
  N21: Bauteil2.A1, Bauteil8.A1, C2.+, R1.Pin_0
  N22: Bauteil2.A0, Bauteil8.A0, C1.+, R5.Pin_0
  N23: Bauteil2.AREF, Bauteil8.AREF
  3V3: Bauteil2.3V3, Bauteil8.3V3
  N24: Bauteil2.D13/SCK, Bauteil8.D13/SCK
  N25: Bauteil3.OUT, R4.Pin_0
  N26: Bauteil4.OUT, R1.Pin_1
  N27: Bauteil5.OUT, R3.Pin_0
  N28: Bauteil6.OUT, R2.Pin_1
  N29: Bauteil7.OUT, R5.Pin_1

notes:
  small capacitors are 470nF, resistors 68 ohm

custom parts:
  Adafruit MAX4466 Electret Microphone Amplifier: Add an ear to your project with this well-designed electret microphone amplifier. This fully assembled and tested board comes with a 20-20KHz electret microphone soldered on. For the amplification, we use the Maxim MAX4466, an op-amp specifically designed for this delicate task! The amplifier has excellent power supply noise rejection, so this amplifier sounds really good and isn't nearly as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
